# Fritzing sketch dcmotorpotansiyometre (saved by Fritzing 0.9.3b)
breadboards: 1

parts:
  Parça1 = Arduino Uno (Rev3) - ICSP
  R2 = Resistor [tolerance=±5% resistance=220 package=THT]
  D1 = Rectifier Diode [part_number=1N4001 package="Melf DO-213 AB [SMD]"]
  Q1 = NPN-Transistor [package="TO92 [THT]"]
  M1 = DC Motor
  U1 = POT [package=pot_alpha_rv16af-20]

nets:
  N1: Parça1.D3_PWM, R2.Pin_1
  N2: Parça1.5V, U1.A
  N3: Parça1.GND, Q1.C, U1.E
  N4: Parça1.VIN, D1.cathode, M1.pin_1
  N5: R2.Pin_0, D1.anode, Q1.E, M1.pin_2
